# Fritzing sketch פריצינג סופי של הפרוייקט (saved by Fritzing 0.9.3b)
breadboards: 3

parts:
  Part1 = Arduino Mega ADK (Rev3)
  U1 = ESP8266 WiFi Module [part_number=ESP8266]
  KY-1 = TONGLING Relay [package=THT]
  KY-2 = TONGLING Relay [package=THT]
  KY-3 = TONGLING Relay [package=THT]
  KY-4 = TONGLING Relay [package=THT]
  F1 = FUSE [package=fuse_5mm]
  BAT1 = BC9VPC [package=bc9vpc]
  R1 = Resistor [tolerance=±5% resistance=220 package=THT]
  R2 = Resistor [tolerance=±5% resistance=220 package=THT]
  D1 = Rectifier Diode [part_number=1N4001 package="300 mil [THT]"]
  J2 = Screw terminal - 2 pins [package=THT]
  R3 = Resistor [tolerance=±5% resistance=220 package=THT]
  R4 = Resistor [tolerance=±5% resistance=220 package=THT]
  J3 = Screw terminal - 2 pins [package=THT]
  J4 = Screw terminal - 2 pins [package=THT]
  J5 = Screw terminal - 2 pins [package=THT]
  D2 = Rectifier Diode [part_number=1N4001 package="300 mil [THT]"]
  D3 = Rectifier Diode [part_number=1N4001 package="300 mil [THT]"]
  J6 = Screw terminal - 2 pins [package=THT]
  R5 = Resistor [tolerance=±5% resistance=220 package=THT]
  R6 = Resistor [tolerance=±5% resistance=220 package=THT]
  R7 = Resistor [tolerance=±5% resistance=220 package=THT]
  R8 = Resistor [tolerance=±5% resistance=220 package=THT]
  S1 = Pushbutton [package="[THT]"]
  S2 = Pushbutton [package="[THT]"]
  R9 = Resistor [tolerance=±5% resistance=220 package=THT]
  R10 = Resistor [tolerance=±5% resistance=220 package=THT]
  Tiny_RTC1 = Tiny RTC
  Mod1 = KY-015 Temperature & Humidity Sensor Module [package="Breakout board"]
  Mod2 = KY-015 Temperature & Humidity Sensor Module [package="Breakout board"]
  Mod3 = KY-015 Temperature & Humidity Sensor Module [package="Breakout board"]
  R11 = Resistor [tolerance=±5% resistance=220 package=THT]
  R12 = Photocell (LDR) [package=THT]
  R13 = Photocell (LDR) [package=THT]
  R14 = Photocell (LDR) [package=THT]
  R15 = Resistor [tolerance=±5% resistance=220 package=THT]
  R16 = Resistor [tolerance=±5% resistance=220 package=THT]

nets:
  N1: Part1.A8, R14.pin_0, R16.Pin_1
  N2: Part1.A0, R3.Pin_1, R4.Pin_0
  N3: Part1.A1, R1.Pin_0, R2.Pin_0
  N4: Part1.A4, R5.Pin_0, R6.Pin_1
  N5: Part1.A5, R7.Pin_0, R8.Pin_1
  N6: Part1.A7, R13.pin_0, R15.Pin_1
  N7: Part1.D21/SCL, Tiny_RTC1.SCL#1
  N8: Part1.D20/SDA, Tiny_RTC1.SDA#2
  N9: Part1.D15/RX3, U1.RXD
  N10: Part1.D14/TX3, U1.TXD
  GND: Part1.GND, U1.GND, R4.Pin_1, R5.Pin_1, R7.Pin_1, S1.Pin_3, S1.Pin_4, S2.Pin_3, S2.Pin_4, R9.Pin_1, R10.Pin_1, Tiny_RTC1.GND#4, Mod1.-, Mod2.-, Mod3.-, R12.pin_1, R13.pin_1, R14.pin_1
  N11: Part1.D12_PWM, S2.Pin_1, S2.Pin_2
  N12: Part1.D11_PWM, S1.Pin_1, S1.Pin_2
  3V3: Part1.3V3, U1.VCC
  VIN: Part1.5V, R9.Pin_0, R10.Pin_0, Tiny_RTC1.VCC#3, Mod1.Vin, Mod2.Vin, Mod3.Vin, R11.Pin_0, R15.Pin_0, R16.Pin_0
  N13: Part1.D22, Mod1.S
  N14: Part1.D23, Mod2.S
  N15: Part1.D24, Mod3.S
  N16: KY-1.C, KY-2.C, KY-3.C, BAT1.V-, R2.Pin_1, J6.pin2
  N17: KY-1.NO, J2.pin2, R3.Pin_0
  N18: KY-2.NO, J4.pin2
  N19: KY-3.NO, J3.pin2, R6.Pin_0
  N20: KY-4.NC, J6.pin1
  N21: KY-4.C, F1.2, BAT1.V+, R1.Pin_1, D2.anode, D3.anode
  N22: KY-4.NO, J5.pin2
  N23: F1.1, D1.anode
  N24: D1.cathode, J2.pin1
  N25: J3.pin1, D2.cathode
  N26: J4.pin1, D3.cathode
  N27: R11.Pin_1, R12.pin_0

custom parts:
  ESP8266 WiFi Module: Generic WiFi Module based on the ESP8266 with onboard PCB antenna and UART communications
  TONGLING Relay: The TONGLING 5V relay module is suitable for SCM development, home appliance control. It uses a 5V~12V TIL control signal which can control DC / AC signal.
  Tiny RTC: Tiny RTC I2C module DS1370Z RTC and AT24C32 EEPROM
  KY-015 Temperature & Humidity Sensor Module: KY-015 temperature and humidity sensor module, provides a low-latency serial interface to measure humidity and temperature.
